// Logisim project multiplication-division.circ as structural Verilog: 3 circuits, main circuit main
module main (
  input  Random_8_bits,
  input  [15:0] Operand_1__Multiplicand_or_Dividend,
  input  [15:0] Operand_2__Multiplier_and_Divisor,
  input  Mul,
  input  Div,
  output [31:0] Product,
  output M_Ready,
  output [15:0] Quotient,
  output [15:0] Remainder__lo,
  output D_Ready
);

  wire and_1_out, and_2_out, and_3_out, Clock_out, multiplexer_1_out, multiplexer_4_out, not_1_out, or_1_out;
  wire [7:0] random_1_out, random_2_out;
  wire [15:0] multiplexer_2_out, multiplexer_3_out;

  // Probe on Operand_1__Multiplicand_or_Dividend
  // Probe on Operand_2__Multiplier_and_Divisor
  Clock Clock (.out(Clock_out));
  LED Ready (.in(and_1_out));
  Random random_1 (.clk(Random_8_bits), .out(random_1_out));  // open: next, clr
  // Probe on random_2_out
  // Probe on random_1_out
  or or_1 (or_1_out, Mul, Div);
  and and_1 (and_1_out, or_1_out, multiplexer_4_out, multiplexer_1_out);
  Multiplexer multiplexer_1 (.in0(1'b1), .in1(and_3_out), .out(multiplexer_1_out), .sel(Div));  // open: en
  Random #(.seed(1)) random_2 (.clk(Random_8_bits), .out(random_2_out));  // open: next, clr
  not not_1 (not_1_out, Random_8_bits);
  Multiplexer #(.width(16)) multiplexer_2 (
    .in0({{8{1'b0}}, random_2_out}), .in1(Operand_1__Multiplicand_or_Dividend), .out(multiplexer_2_out),
    .sel(not_1_out));  // open: en
  Multiplexer #(.width(16)) multiplexer_3 (
    .in0({{8{1'b0}}, random_1_out}), .in1(Operand_2__Multiplier_and_Divisor), .out(multiplexer_3_out),
    .sel(not_1_out));  // open: en
  Multiplexer multiplexer_4 (.in0(1'b1), .in1(and_2_out), .out(multiplexer_4_out), .sel(Mul));  // open: en
  and and_2 (and_2_out, Mul, M_Ready);
  and and_3 (and_3_out, Div, D_Ready);
  _16_bit_Multiplication u_16_bit_multiplication_1 (
    .Multiplicand(multiplexer_2_out), .Multiplier(multiplexer_3_out), .Mul(Mul), .Product(Product),
    .M_Ready(M_Ready), .Clock(Clock_out));
  _16_bit_Division u_16_bit_division_1 (
    .Divisor(multiplexer_3_out), .Dividend(multiplexer_2_out), .Div(Div), .Quotient(Quotient),
    .Remainder__lo(Remainder__lo), .D_Ready(D_Ready), .Clock(Clock_out));
  // Probe on Product
  // Probe on Quotient
  // Probe on Remainder__lo

  // Notes on the sheet:
  //   allows parellel ops
  //   and starting independently
  //   able to do 2nd op with different numbers
endmodule

module _16_bit_Division (
  input  [15:0] Divisor,
  input  [15:0] Dividend,
  input  Div,
  input  Clock,
  output [15:0] Quotient,
  output [15:0] Remainder__lo,
  output D_Ready
);

  wire and_1_out, and_2_out, chk_Div_return_out, comparator_1_eq, comparator_2_lt, comparator_3_lt,
       comparator_4_eq, comparator_4_lt, comparator_5_lt, comparator_6_gt, comparator_7_eq, comparator_7_gt,
       comparator_7_lt, comparator_8_eq, comparator_8_lt, counter_1_carry, div_1_out, even_carry,
       is_D_Ready_out, LSB_odd_chk_out, multiplexer_6_out, nor_1_out, not_1_out, not_2_out, not_3_out,
       odd_carry, or_1_out, or_2_out;
  wire [7:0] counter_1_q;
  wire [15:0] adder_2_out, multiplexer_1_out, multiplexer_2_out, multiplexer_7_out, multiplexer_8_out,
       shifter_2_out;
  wire [31:0] adder_1_out, Divisor_q, multiplexer_3_out, multiplexer_4_out, multiplexer_5_out,
       multiplexer_9_out, multiplexer_10_out, shifter_1_out, subtractor_1_out;
  wire [31:16] Remainder_q;

  // Probe on Divisor
  // Probe on Dividend
  Comparator #(.width(16), .mode("unsigned")) comparator_1 (
    .a(16'h1), .b(Divisor), .eq(comparator_1_eq));  // open: gt, lt
  Multiplexer #(.width(16)) multiplexer_1 (
    .in0(Divisor), .in1({16{1'b0}}), .out(multiplexer_1_out), .sel(comparator_2_lt));  // open: en
  Multiplexer #(.width(16)) multiplexer_2 (
    .in0(Dividend), .in1({16{1'b0}}), .out(multiplexer_2_out), .sel(comparator_2_lt));  // open: en
  Comparator #(.mode("unsigned")) comparator_2 (.a(8'h1), .b(counter_1_q), .lt(comparator_2_lt));  // open: gt, eq
  Counter #(.ongoal("stay")) counter_1 (
    .Q(counter_1_q), .carry(counter_1_carry), .clk(and_1_out), .clr(not_1_out));  // open: load, D, count
  not not_1 (not_1_out, Div);
  and and_1 (and_1_out, Div, Clock);
  Multiplexer #(.width(32)) multiplexer_3 (
    .in0({multiplexer_1_out, {16{1'b0}}}), .in1(shifter_1_out), .out(multiplexer_3_out), .sel(comparator_2_lt));  // open: en
  Multiplexer #(.width(32)) multiplexer_4 (
    .in0({{16{1'b0}}, multiplexer_2_out}), .in1(multiplexer_10_out), .out(multiplexer_4_out),
    .sel(comparator_2_lt));  // open: en
  Comparator #(.mode("unsigned")) comparator_3 (.a(8'h2), .b(counter_1_q), .lt(comparator_3_lt));  // open: gt, eq
  Shifter #(.width(32), .shift("lr")) shifter_1 (.in(Divisor_q), .\dist (5'b00001), .out(shifter_1_out));
  Register #(.width(32)) u_Divisor (
    .D(multiplexer_3_out), .en(nor_1_out), .Q(Divisor_q), .clk(and_1_out), .clr(not_1_out));
  Register #(.width(32)) Remainder (
    .D(multiplexer_4_out), .en(nor_1_out), .Q({Remainder_q, Remainder__lo}), .clk(and_1_out), .clr(not_1_out));
  Multiplexer #(.width(32)) multiplexer_5 (
    .in0(32'h1), .in1(32'h2), .out(multiplexer_5_out), .sel(Divisor[0]));  // open: en
  Subtractor #(.width(32)) subtractor_1 (
    .a({Remainder_q, Remainder__lo}), .b(Divisor_q), .out(subtractor_1_out));  // open: bin, bout
  Comparator #(.width(32), .mode("unsigned")) comparator_4 (
    .a(Divisor_q), .b(multiplexer_5_out), .eq(comparator_4_eq), .lt(comparator_4_lt));  // open: gt
  Comparator #(.width(16)) comparator_5 (.a(Divisor_q[15:0]), .b(Divisor), .lt(comparator_5_lt));  // open: gt, eq
  Comparator #(.width(16)) comparator_6 (.a(Divisor), .b(Dividend), .gt(comparator_6_gt));  // open: eq, lt
  or or_1 (or_1_out, comparator_7_gt, comparator_7_eq);
  Comparator #(.width(32)) comparator_7 (
    .a(subtractor_1_out), .b({32{1'b0}}), .gt(comparator_7_gt), .eq(comparator_7_eq), .lt(comparator_7_lt));
  Adder #(.width(32)) adder_1 (.a(subtractor_1_out), .b(Divisor_q), .out(adder_1_out));  // open: cin, cout
  and div_1 (div_1_out, comparator_3_lt, comparator_1_eq);
  Multiplexer multiplexer_6 (
    .in0(even_carry), .in1(odd_carry), .out(multiplexer_6_out), .sel(LSB_odd_chk_out));  // open: en
  and LSB_odd_chk (LSB_odd_chk_out, Dividend[0], Divisor[0]);
  Multiplexer #(.width(16)) multiplexer_7 (
    .in0(shifter_2_out), .in1(adder_2_out), .out(multiplexer_7_out), .sel(or_1_out));  // open: en
  Multiplexer #(.width(16)) multiplexer_8 (
    .in0(multiplexer_7_out), .in1(Dividend), .out(multiplexer_8_out), .sel(comparator_1_eq));  // open: en
  Multiplexer #(.width(32)) multiplexer_9 (
    .in0(subtractor_1_out), .in1(adder_1_out), .out(multiplexer_9_out), .sel(comparator_7_lt));  // open: en
  Multiplexer #(.width(32)) multiplexer_10 (
    .in0(multiplexer_9_out), .in1({32{1'b0}}), .out(multiplexer_10_out), .sel(comparator_1_eq));  // open: en
  or chk_Div_return (chk_Div_return_out, div_1_out, comparator_4_lt, comparator_4_eq, counter_1_carry, multiplexer_6_out);
  not not_2 (not_2_out, not_1_out);
  or or_2 (or_2_out, comparator_8_eq, comparator_8_lt);
  Comparator #(.width(16), .mode("unsigned")) comparator_8 (
    .a({16{1'b0}}), .b(Divisor), .eq(comparator_8_eq), .lt(comparator_8_lt));  // open: gt
  Register #(.width(16)) u_Quotient (
    .D(multiplexer_8_out), .en(nor_1_out), .Q(Quotient), .clk(and_1_out), .clr(not_3_out));
  not not_3 (not_3_out, comparator_2_lt);
  nor nor_1 (nor_1_out, and_2_out, comparator_4_eq, is_D_Ready_out);
  and is_D_Ready (is_D_Ready_out, comparator_2_lt, chk_Div_return_out, not_2_out, or_2_out);
  Counter #(.width(2), .max('h1), .ongoal("load")) even (
    .carry(even_carry), .clk(comparator_5_lt), .clr(not_1_out));  // open: load, D, count, Q
  Counter #(.width(2), .max('h2), .ongoal("load")) odd (
    .carry(odd_carry), .clk(comparator_5_lt), .clr(not_1_out));  // open: load, D, count, Q
  Adder #(.width(16)) adder_2 (.a(16'h1), .b(shifter_2_out), .out(adder_2_out));  // open: cin, cout
  Shifter #(.width(16)) shifter_2 (.in(Quotient), .\dist (4'b0001), .out(shifter_2_out));
  // Probe on Quotient
  // Probe on Remainder_q
  // Probe on Remainder__lo
  and and_2 (and_2_out, comparator_2_lt, comparator_6_gt);
  or or_3 (D_Ready, is_D_Ready_out, and_2_out);

  // Notes on the sheet:
  //   if divide by 1 skip all the steps
  //   Load Data if pc<1
  //   Load Upper
  //   Load Lower
  //   div/1 in 3 cycles
  //   reset if Div=0
  //   Clock to Registers
  //   unused:if div odd stop@2||even stop@1
  //   chk LSB
  //   $divisor < divisor
  //   divisor > dividend
  //   Test Remainder<0
  //   restore remainder
  //   no divide by zero or less
  //   write disable
  //   count when divisor done based on odd parity
endmodule

module _16_bit_Multiplication (
  input  [15:0] Multiplicand,
  input  [15:0] Multiplier,
  input  Mul,
  input  Clock,
  output [31:0] Product,
  output M_Ready
);

  wire and_1_out, comparator_1_lt, comparator_2_eq, counter_1_carry, M2_0____pc_out, not_1_out, not_2_out,
       not_3_out, not_4_out;
  wire [7:0] counter_1_q;
  wire [15:0] multiplexer_1_out, multiplexer_2_out, multiplexer_4_out, Multiplier_q, shifter_2_out;
  wire [31:0] adder_1_out, multiplexer_3_out, multiplexer_5_out, Multiplicand_q, shifter_1_out;

  // Probe on Multiplicand
  // Probe on Multiplier
  Multiplexer #(.width(16)) multiplexer_1 (
    .in0(Multiplicand), .in1({16{1'b0}}), .out(multiplexer_1_out), .sel(comparator_1_lt));  // open: en
  Multiplexer #(.width(16)) multiplexer_2 (
    .in0(Multiplier), .in1({16{1'b0}}), .out(multiplexer_2_out), .sel(comparator_1_lt));  // open: en
  Comparator #(.mode("unsigned")) comparator_1 (.a(8'h1), .b(counter_1_q), .lt(comparator_1_lt));  // open: gt, eq
  Counter #(.ongoal("stay")) counter_1 (
    .Q(counter_1_q), .carry(counter_1_carry), .clk(and_1_out), .clr(not_1_out));  // open: load, D, count
  not not_1 (not_1_out, Mul);
  and and_1 (and_1_out, Mul, Clock);
  Multiplexer #(.width(32)) multiplexer_3 (
    .in0({{16{1'b0}}, multiplexer_1_out}), .in1(shifter_1_out), .out(multiplexer_3_out), .sel(comparator_1_lt));  // open: en
  Multiplexer #(.width(16)) multiplexer_4 (
    .in0(multiplexer_2_out), .in1(shifter_2_out), .out(multiplexer_4_out), .sel(comparator_1_lt));  // open: en
  Register #(.width(32)) u_Multiplicand (
    .D(multiplexer_3_out), .Q(Multiplicand_q), .clk(and_1_out), .clr(not_1_out));  // open: en
  Register #(.width(16)) u_Multiplier (
    .D(multiplexer_4_out), .Q(Multiplier_q), .clk(and_1_out), .clr(not_1_out));  // open: en
  Shifter #(.width(32)) shifter_1 (.in(Multiplicand_q), .\dist (5'b00001), .out(shifter_1_out));
  Shifter #(.width(16), .shift("lr")) shifter_2 (.in(Multiplier_q), .\dist (4'b0001), .out(shifter_2_out));
  not not_2 (not_2_out, not_1_out);
  Multiplexer #(.width(32)) multiplexer_5 (
    .in0({32{1'b0}}), .in1(Multiplicand_q), .out(multiplexer_5_out), .sel(Multiplier_q[0]));  // open: en
  Comparator #(.width(16), .mode("unsigned")) comparator_2 (
    .a(Multiplier_q), .b({16{1'b0}}), .eq(comparator_2_eq));  // open: gt, lt
  Adder #(.width(32)) adder_1 (.a(multiplexer_5_out), .b(Product), .out(adder_1_out));  // open: cin, cout
  or M2_0____pc (M2_0____pc_out, comparator_2_eq, counter_1_carry);
  not not_3 (not_3_out, M_Ready);
  not not_4 (not_4_out, comparator_1_lt);
  and is_M_Ready (M_Ready, comparator_1_lt, M2_0____pc_out, not_2_out);
  Register #(.width(32)) u_Product (.D(adder_1_out), .en(not_3_out), .Q(Product), .clk(and_1_out), .clr(not_4_out));
  // Probe on Product

  // Notes on the sheet:
  //   Load Data if pc<1
  //   Load Lower
  //   reset if Mul=0
  //   Clock to Registers
endmodule
